# Fritzing sketch Arduino.GPS (saved by Fritzing 0.9.4)
breadboards: 1

parts:
  Part1 = Arduino Uno (Rev3)
  Part2 = Adafruit Ultimate GPS v3 [part_number="Adafruit #746"]

nets:
  GND: Part1.GND, Part2.GND
  N1: Part1.D0/RX, Part2.TX
  5V: Part1.5V, Part2.VIN

custom parts:
  Adafruit Ultimate GPS v3: We carry a few different GPS modules here in the Adafruit shop, but none that satisfied our every desire - that's why we designed this little GPS breakout board. We believe this is the Ultimate GPS module, so we named it that. It's got everything you want and more: -165 dBm sensitivity, 10 Hz updates, 66 channels 5V friendly design and only 20mA current draw Breadboard friendly + two mounting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

// code stored in the sketch: Arduino.GPS.ino

