# Fritzing sketch Feedback.Servo (saved by Fritzing 0.9.3b)

parts:
  Part1 = Adafruit Metro with Headers [part_number="Adafruit #2488"]
  SERVO1 = Adafruit Feedback Servo (small)

nets:
  N1: Part1.AD0, SERVO1.Feedback
  N2: Part1.IO9, SERVO1.Signal
  N3: Part1.+5V, SERVO1.Power
  N4: Part1.GND, SERVO1.Ground

custom parts:
  Adafruit Metro with Headers: We sure love the ATmega328 here at Adafruit, and we use them a lot for our own projects. The processor has plenty of GPIO, Analog inputs, hardware UART SPI and I2C, timers and PWM galore - just enough for most simple projects. When we need to go small, we use a Pro Trinket 3V or 5V, but when size isn't as much of a concern, and an USB-serial converter is required, we reach for an Adafruit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
  Adafruit Feedback Servo (small): Adafruit Feedback Servo (Small)

// code stored in the sketch: feedback.servo.ino
#include <Servo.h> 
 
Servo feedbackServo;  

// Control and feedback pins
const int SERVO_PIN    = 9;
const int FEEDBACK_PIN = A0;

// Calibration values
int minDegrees;
int maxDegrees;
int minFeedback;
int maxFeedback;
int tolerance = 2; // max feedback measurement error

/*
  This function establishes the feedback values for 2 positions of the servo.
  With this information, we can interpolate feedback values for intermediate positions
*/
void calibrate(Servo servo, int analogPin, int minPos, int maxPos) {
  // Move to the minimum position and record the feedback value
  Serial.println("Min pos");
  servo.write(minPos);
  minDegrees = minPos;
  delay(1000); // make sure it has time to get there and settle
  minFeedback = analogRead(analogPin);
  
  // Move to the maximum position and record the feedback value
  Serial.println("Max pos");
  servo.write(maxPos);
  maxDegrees = maxPos;
  delay(2000); // make sure it has time to get there and settle
  maxFeedback = analogRead(analogPin);
}

int getPos(int analogPin) {
  return map(analogRead(analogPin), minFeedback, maxFeedback, minDegrees, maxDegrees);
}
 
void setup() { 
  Serial.begin(9600);
  
  feedbackServo.attach(SERVO_PIN); 
  calibrate(feedbackServo, FEEDBACK_PIN, 20, 160);  // calibrate for the 20-160 degree range
  feedbackServo.detach(); // To free it, can be moved by hand.
  Serial.println("Servo is now free, move it by hand");
} 

void loop() {
  delay(5000);
  int pos = getPos(FEEDBACK_PIN);
  Serial.print("Pos:");
  Serial.println(pos);
}
