# Fritzing sketch TCP.watch.feather.128x32 (saved by Fritzing 0.9.3b)

parts:
  Part1 = Adafruit Feather HUZZAH ESP8266 [part_number="Adafruit #2821"]
  Part3 = Lithium Ion Polymer Battery 3.7v 350mAh [part_number=2750]  # not connected
  Part4 = Adafruit OLED FeatherWing [part_number="Adafruit #2900"]

nets:
  GND: Part1.GND, Part4.GND
  3.3V: Part1.3.3V, Part4.3.3V
  N1: Part1.GPIO5/SCL, Part4.SCL
  N2: Part1.GPIO4/SDA, Part4.SDA

notes:
  Use stack headers to stack the screen on top of the feather with ESP8266

custom parts:
  Adafruit Feather HUZZAH ESP8266: his is the Adafruit Feather HUZZAH ESP8266 - our take on an 'all-in-one' ESP8266 WiFi development board with built in USB and battery charging. Its an ESP8266 WiFi module with all the extras you need, ready to rock! We have other boards in the Feather family, check'em out here. At the Feather HUZZAH's heart is an ESP8266 WiFi microcontroller clocked at 80 MHz and at 3.3V logic. This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
  Lithium Ion Polymer Battery 3.7v 350mAh: Lithium ion polymer (also known as 'lipo' or 'lipoly') batteries are thin, light and powerful. The output ranges from 4.2V when completely charged to 3.7V. This battery has a capacity of 350mAh for a total of about 1.3 Wh. The batteries come pre-attached with a genuine 2-pin JST-PH connector as shown and include the necessary protection circuitry.
  Adafruit OLED FeatherWing: This is the FeatherWing OLED: it adds a 128x32 monochrome OLED plus 3 user buttons to any Feather main board. These displays are small, only about 1" diagonal, but very readable due to the high contrast of an OLED display. This screen is made of 128x32 individual white OLED pixels and because the display makes its own light, no backlight is required. This reduces the power required to run the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
