# Fritzing sketch RasPi.led (saved by Fritzing 0.9.4)

parts:
  R1 = Resistor [tolerance=±5% resistance=220 package=THT]
  LED1 = LED - 5mm [color="Red (633nm)" package="5 mm [THT]"]
  Raspberry_Pi1 = Raspberry Pi 2

nets:
  N1: R1.Pin_1, Raspberry_Pi1.GPIO18
  N2: LED1.cathode, Raspberry_Pi1.GND

notes:
  220 Ohms
