# Fritzing sketch RPi.GPS (saved by Fritzing 0.9.4)
breadboards: 1

parts:
  Raspberry_Pi_1 = Raspberry Pi 3 [part_number=RPI-3-V1.2]
  Part1 = Adafruit Ultimate GPS v3 [part_number="Adafruit #746"]

nets:
  N1: Raspberry_Pi_1.GPIO15, Part1.TX
  GND: Raspberry_Pi_1.GND, Part1.GND
  5V: Raspberry_Pi_1.5V, Part1.VIN

notes:
  No need here for the GPS to receive anything.
  GPS's Tx goes to RPi's Rx

custom parts:
  Adafruit Ultimate GPS v3: We carry a few different GPS modules here in the Adafruit shop, but none that satisfied our every desire - that's why we designed this little GPS breakout board. We believe this is the Ultimate GPS module, so we named it that. It's got everything you want and more: -165 dBm sensitivity, 10 Hz updates, 66 channels 5V friendly design and only 20mA current draw Breadboard friendly + two mounting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
